# Fritzing sketch Design_2 (saved by Fritzing 0.8.7b)
breadboards: 1

parts:
  Raspberry_Pi_Zero1 = Raspberry Pi Zero
  M1 = 5-ir-array-sensor [package=THT]
  Part1 = Adafruit PowerBoost 1000C [part_number="Adafruit #2465"]
  BATT1 = LiPoly Battery (1300mAh)
  M2 = DC Motor
  M4 = DC Motor
  X1 = USB Connectors [package=usb-a-h]
  BATT2 = LiPoly Battery (1300mAh)
  S1 = SWITCH-MOMENTARY-2 [package=tactile-switch-1101ne]
  S2 = SWITCH-MOMENTARY-2 [package=tactile-switch-1101ne]
  M5 = L293D Motor Driver

nets:
  N1: Raspberry_Pi_Zero1.GIPO9, M1.VCC
  N2: Raspberry_Pi_Zero1.GIPO5, M1.S5
  N3: Raspberry_Pi_Zero1.GIPO6, M1.S4
  N4: Raspberry_Pi_Zero1.GIPO13, M1.S3
  N5: Raspberry_Pi_Zero1.GIPO19, M1.S2
  GND: Raspberry_Pi_Zero1.GIPO26, Raspberry_Pi_Zero1.GND, M1.S1, M1.GND, Part1.GND, X1.GND, BATT2.negative
  N6: Raspberry_Pi_Zero1.5V, S1.1
  N7: Part1.VBUS, X1.D+, S2.1
  N8: Part1.VLIPO, BATT1.positive
  N9: Part1.ENABLE, BATT1.negative
  N10: Part1.5.0V, S1.2
  N11: M2.pin_1, M2.pin_2, M4.pin_1, M4.pin_2, BATT2.positive, S2.2, M5.pin_9, M5.pin_10, M5.pin_11, M5.pin_12

custom parts:
  5-ir-array-sensor: 5 IR array sensor.
  Adafruit PowerBoost 1000C: PowerBoost 1000C is the perfect power supply for your portable project! With a built-in load-sharing battery charger circuit, you'll be able to keep your power-hungry project running even while recharging the battery! This little DC/DC boost converter module can be powered by any 3.7V LiIon/LiPoly battery, and convert the battery output to 5.2V DC for running your 5V projects.
  LiPoly Battery (1300mAh): Lithium Ion Polymer Battery (1300mAh)
